// Logisim project TBX32.circ as structural Verilog: 6 circuits, main circuit RegisterFile
module CPU (
  input  in_1,
  input  in_2,
  input  in_3,
  input  [2:0] in_4,
  input  [1:0] in_5,
  input  [1:0] in_6,
  input  [1:0] in_7,
  input  [2:0] in_8,
  input  in_9,
  input  in_10,
  input  in_11,
  input  in_12,
  input  in_13,
  input  in_14,
  input  in_15
);

  wire ALUADRBUS_OUT, ALUDATBUS_OUT, CLOCK, comparator_1_eq, comparator_1_gt, comparator_1_lt, IR_LD, MAR_LD,
       MEM_LD, MEM_OUT, not_1_out, or_1_out, PC_LD, PCADRBUS_OUT, RA_SEL, RF_LD, RST;
  wire [1:0] ALUFUN_SEL, PCDATA_SEL, PCMODE_SEL;
  wire [2:0] BBUS_SEL, PCCOND_SEL;
  wire [3:0] ir_1_alufunction, multiplexer_1_out;
  wire [4:0] controlled_buffer_1_out, ir_1_ra, ir_1_rb, ir_1_rc;
  wire [5:0] ir_1_opcode;
  wire [10:0] ir_1_xtdopcode;
  wire [15:0] ir_1_offset;
  wire [20:0] bit_extender_4_out, ir_1_address;
  wire [31:0] alu_1_output, bit_extender_1_out, bit_extender_2_out, bit_extender_3_out,
       controlled_buffer_3_out, controlled_buffer_4_out, controlled_buffer_6_out, ir_1_q, MAR_q,
       multiplexer_2_out, multiplexer_3_out, pc_1_q, random_1_out, registerfile_1_output__1,
       registerfile_1_output__2;
  wire [31:22] controlunit_1_q;

  buf buffer_1 (IR_LD, in_1);
  // Probe on ir_1_xtdopcode
  // Probe on ir_1_opcode
  buf buffer_2 (RA_SEL, in_2);
  ControlUnit controlunit_1 (
    .OpCode(ir_1_opcode), .XtdOpCode(ir_1_xtdopcode), .Clk(CLOCK), ._0(RST),
    .Q({controlunit_1_q, IR_LD, RA_SEL, RF_LD, BBUS_SEL, ALUFUN_SEL, PCDATA_SEL, PCMODE_SEL, PCCOND_SEL, PC_LD, ALUADRBUS_OUT, ALUDATBUS_OUT, PCADRBUS_OUT, MAR_LD, MEM_LD, MEM_OUT}));
  IR ir_1 (
    .D(controlled_buffer_4_out), .OpCode(ir_1_opcode), .RA(ir_1_ra), .RB(ir_1_rb), .RC(ir_1_rc),
    .Address(ir_1_address), .Offset(ir_1_offset), .XtdOpCode(ir_1_xtdopcode), .AluFunction(ir_1_alufunction),
    .Enable(IR_LD), .Clock(CLOCK), .Q(ir_1_q));
  buf buffer_3 (RF_LD, in_3);
  not not_1 (not_1_out, RA_SEL);
  assign controlled_buffer_1_out = RA_SEL ? ir_1_ra : 5'bz;  // Controlled_Buffer controlled_buffer_1
  assign controlled_buffer_1_out = not_1_out ? ir_1_rb : 5'bz;  // Controlled_Buffer controlled_buffer_2
  assign bit_extender_1_out = {{11{1'b0}}, ir_1_address};  // Bit_Extender bit_extender_1
  assign BBUS_SEL = in_4;  // Buffer buffer_4, 3 bits wide
  // Probe on ir_1_q
  // Probe on ir_1_ra
  // Probe on controlled_buffer_1_out
  // Probe on ir_1_rc
  // Probe on controlled_buffer_4_out
  assign ALUFUN_SEL = in_5;  // Buffer buffer_5, 2 bits wide
  Clock clock_1 (.out(CLOCK));
  Button Reset (.out(RST));
  RegisterFile registerfile_1 (
    .Data(controlled_buffer_4_out), .Write_Selector(ir_1_ra), .Write_Enable(RF_LD),
    .Output__1(registerfile_1_output__1), .Output__2(registerfile_1_output__2),
    .Read__1_Selector(controlled_buffer_1_out), .Clock(CLOCK), .Read__2_Selector(ir_1_rc));
  assign PCDATA_SEL = in_6;  // Buffer buffer_6, 2 bits wide
  // Probe on registerfile_1_output__1
  // Probe on registerfile_1_output__2
  assign bit_extender_2_out = {{16{1'b0}}, ir_1_offset};  // Bit_Extender bit_extender_2
  assign bit_extender_3_out = {{16{ir_1_offset[15]}}, ir_1_offset};  // Bit_Extender bit_extender_3
  assign PCMODE_SEL = in_7;  // Buffer buffer_7, 2 bits wide
  // Probe on {controlunit_1_q, IR_LD, RA_SEL, RF_LD, BBUS_SEL, ALUFUN_SEL, PCDATA_SEL, PCMODE_SEL, PCCOND_SEL, PC_LD, ALUADRBUS_OUT, ALUDATBUS_OUT, PCADRBUS_OUT, MAR_LD, MEM_LD, MEM_OUT}
  Random #(.width(32)) random_1 (.clk(CLOCK), .out(random_1_out));  // open: next, clr
  // Probe on bit_extender_1_out
  // Probe on bit_extender_3_out
  Multiplexer #(.select(2), .width(4), .enable("false")) multiplexer_1 (
    .in0(ir_1_alufunction), .in1(4'b0001), .in2(4'b1110), .in3(4'b1111), .out(multiplexer_1_out),
    .sel(ALUFUN_SEL));
  Multiplexer #(.select(3), .width(32), .enable("false")) multiplexer_2 (
    .in0(registerfile_1_output__2), .in1(bit_extender_2_out), .in2(bit_extender_3_out),
    .in3(bit_extender_1_out), .in4({32{1'b0}}), .in5({32{1'b0}}), .in6({32{1'b0}}), .in7(random_1_out),
    .out(multiplexer_2_out), .sel(BBUS_SEL));
  Multiplexer #(.select(2), .width(32), .enable("false")) multiplexer_3 (
    .in0(alu_1_output), .in1(bit_extender_1_out), .in2(bit_extender_3_out), .in3({32{1'b0}}),
    .out(multiplexer_3_out), .sel(PCDATA_SEL));
  assign PCCOND_SEL = in_8;  // Buffer buffer_8, 3 bits wide
  // Probe on multiplexer_1_out
  // Probe on multiplexer_2_out
  Comparator #(.width(32)) comparator_1 (
    .a(registerfile_1_output__1), .b(multiplexer_2_out), .gt(comparator_1_gt), .eq(comparator_1_eq),
    .lt(comparator_1_lt));
  buf buffer_9 (PC_LD, in_9);
  ALU alu_1 (
    .Input__1(registerfile_1_output__1), .Output(alu_1_output), .Input__2(multiplexer_2_out),
    .Function(multiplexer_1_out));
  PC pc_1 (
    .Address(multiplexer_3_out), .Q(pc_1_q), .Load_Select(PCMODE_SEL), .Clock(CLOCK),
    .Greater(comparator_1_gt), .Equal(comparator_1_eq), .Less(comparator_1_lt),
    .Condition_Select(PCCOND_SEL), .Enable(PC_LD), .Reset(RST));
  buf buffer_10 (ALUADRBUS_OUT, in_10);
  // Probe on pc_1_q
  // Probe on controlled_buffer_4_out
  buf buffer_11 (ALUDATBUS_OUT, in_11);
  // Probe on alu_1_output
  assign controlled_buffer_3_out = ALUADRBUS_OUT ? alu_1_output : 32'bz;  // Controlled_Buffer controlled_buffer_3
  assign controlled_buffer_4_out = ALUDATBUS_OUT ? alu_1_output : 32'bz;  // Controlled_Buffer controlled_buffer_4
  assign controlled_buffer_3_out = PCADRBUS_OUT ? pc_1_q : 32'bz;  // Controlled_Buffer controlled_buffer_5
  buf buffer_12 (PCADRBUS_OUT, in_12);
  // Probe on BBUS_SEL
  // Probe on ALUFUN_SEL
  // Probe on controlled_buffer_3_out
  Register #(.width(32)) MAR (.D(controlled_buffer_3_out), .en(MAR_LD), .Q(MAR_q), .clk(CLOCK));  // open: clr
  assign controlled_buffer_6_out = MEM_LD ? controlled_buffer_4_out : 32'bz;  // Controlled_Buffer controlled_buffer_6
  buf buffer_13 (MAR_LD, in_13);
  Bit_Extender #(.in_width(32), .out_width(21)) bit_extender_4 (.in(MAR_q), .out(bit_extender_4_out));
  assign controlled_buffer_4_out = MEM_OUT ? controlled_buffer_6_out : 32'bz;  // Controlled_Buffer controlled_buffer_7
  buf buffer_14 (MEM_LD, in_14);
  // Probe on PCDATA_SEL
  // Probe on MAR_q
  or or_1 (or_1_out, MEM_LD, MEM_OUT);
  buf buffer_15 (MEM_OUT, in_15);
  // Probe on PCMODE_SEL
  RAM #(.addrWidth(21), .dataWidth(32)) ram_1 (
    .addr(bit_extender_4_out), .data(controlled_buffer_6_out), .sel(or_1_out), .clk(CLOCK), .ld(MEM_OUT));  // open: clr
  // Probe on PCCOND_SEL
endmodule

module RegisterFile (
  input  [4:0] Read__1_Selector,
  input  [31:0] Data,
  input  [4:0] Write_Selector,
  input  Write_Enable,
  input  Clock,
  input  [4:0] Read__2_Selector,
  output [31:0] Output__1,
  output [31:0] Output__2
);

  wire decoder_1_out0, decoder_1_out1, decoder_1_out2, decoder_1_out3, decoder_1_out4, decoder_1_out5,
       decoder_1_out6, decoder_1_out7, decoder_1_out8, decoder_1_out9, decoder_1_out10, decoder_1_out11,
       decoder_1_out12, decoder_1_out13, decoder_1_out14, decoder_1_out15, decoder_1_out16, decoder_1_out17,
       decoder_1_out18, decoder_1_out19, decoder_1_out20, decoder_1_out21, decoder_1_out22, decoder_1_out23,
       decoder_1_out24, decoder_1_out25, decoder_1_out26, decoder_1_out27, decoder_1_out28, decoder_1_out29,
       decoder_1_out30, decoder_1_out31;
  wire [31:0] R00out, R01out, R02out, R03out, R04out, R05out, R06out, R07out, R08out, R09out, R10out, R11out,
       R12out, R13out, R14out, R15out, R16out, R17out, R18out, R19out, R20out, R21out, R22out, R23out,
       R24out, R25out, R26out, R27out, R28out, R29out, R30out, R31out;

  Register #(.width(32)) register_1 (.D(Data), .en(decoder_1_out0), .Q(R00out), .clk(Clock));  // open: clr
  Register #(.width(32)) register_2 (.D(Data), .en(decoder_1_out1), .Q(R01out), .clk(Clock));  // open: clr
  Register #(.width(32)) register_3 (.D(Data), .en(decoder_1_out2), .Q(R02out), .clk(Clock));  // open: clr
  Register #(.width(32)) register_4 (.D(Data), .en(decoder_1_out3), .Q(R03out), .clk(Clock));  // open: clr
  Register #(.width(32)) register_5 (.D(Data), .en(decoder_1_out4), .Q(R04out), .clk(Clock));  // open: clr
  Register #(.width(32)) register_6 (.D(Data), .en(decoder_1_out5), .Q(R05out), .clk(Clock));  // open: clr
  Register #(.width(32)) register_7 (.D(Data), .en(decoder_1_out6), .Q(R06out), .clk(Clock));  // open: clr
  Register #(.width(32)) register_8 (.D(Data), .en(decoder_1_out7), .Q(R07out), .clk(Clock));  // open: clr
  // Probe on Write_Selector
  Decoder #(.select(5), .disabled(0)) decoder_1 (
    .out0(decoder_1_out0), .out1(decoder_1_out1), .out2(decoder_1_out2), .out3(decoder_1_out3),
    .out4(decoder_1_out4), .out5(decoder_1_out5), .out6(decoder_1_out6), .out7(decoder_1_out7),
    .out8(decoder_1_out8), .out9(decoder_1_out9), .out10(decoder_1_out10), .out11(decoder_1_out11),
    .out12(decoder_1_out12), .out13(decoder_1_out13), .out14(decoder_1_out14), .out15(decoder_1_out15),
    .out16(decoder_1_out16), .out17(decoder_1_out17), .out18(decoder_1_out18), .out19(decoder_1_out19),
    .out20(decoder_1_out20), .out21(decoder_1_out21), .out22(decoder_1_out22), .out23(decoder_1_out23),
    .out24(decoder_1_out24), .out25(decoder_1_out25), .out26(decoder_1_out26), .out27(decoder_1_out27),
    .out28(decoder_1_out28), .out29(decoder_1_out29), .out30(decoder_1_out30), .out31(decoder_1_out31),
    .sel(Write_Selector), .en(Write_Enable));
  Register #(.width(32)) register_9 (.D(Data), .en(decoder_1_out8), .Q(R08out), .clk(Clock));  // open: clr
  Register #(.width(32)) register_10 (.D(Data), .en(decoder_1_out9), .Q(R09out), .clk(Clock));  // open: clr
  Register #(.width(32)) register_11 (.D(Data), .en(decoder_1_out10), .Q(R10out), .clk(Clock));  // open: clr
  Register #(.width(32)) register_12 (.D(Data), .en(decoder_1_out11), .Q(R11out), .clk(Clock));  // open: clr
  Register #(.width(32)) register_13 (.D(Data), .en(decoder_1_out12), .Q(R12out), .clk(Clock));  // open: clr
  Register #(.width(32)) register_14 (.D(Data), .en(decoder_1_out13), .Q(R13out), .clk(Clock));  // open: clr
  Register #(.width(32)) register_15 (.D(Data), .en(decoder_1_out14), .Q(R14out), .clk(Clock));  // open: clr
  Register #(.width(32)) register_16 (.D(Data), .en(decoder_1_out15), .Q(R15out), .clk(Clock));  // open: clr
  Register #(.width(32)) register_17 (.D(Data), .en(decoder_1_out16), .Q(R16out), .clk(Clock));  // open: clr
  Register #(.width(32)) register_18 (.D(Data), .en(decoder_1_out17), .Q(R17out), .clk(Clock));  // open: clr
  Register #(.width(32)) register_19 (.D(Data), .en(decoder_1_out18), .Q(R18out), .clk(Clock));  // open: clr
  Register #(.width(32)) register_20 (.D(Data), .en(decoder_1_out19), .Q(R19out), .clk(Clock));  // open: clr
  Register #(.width(32)) register_21 (.D(Data), .en(decoder_1_out20), .Q(R20out), .clk(Clock));  // open: clr
  Register #(.width(32)) register_22 (.D(Data), .en(decoder_1_out21), .Q(R21out), .clk(Clock));  // open: clr
  Register #(.width(32)) register_23 (.D(Data), .en(decoder_1_out22), .Q(R22out), .clk(Clock));  // open: clr
  Register #(.width(32)) register_24 (.D(Data), .en(decoder_1_out23), .Q(R23out), .clk(Clock));  // open: clr
  Register #(.width(32)) register_25 (.D(Data), .en(decoder_1_out24), .Q(R24out), .clk(Clock));  // open: clr
  Register #(.width(32)) register_26 (.D(Data), .en(decoder_1_out25), .Q(R25out), .clk(Clock));  // open: clr
  Register #(.width(32)) register_27 (.D(Data), .en(decoder_1_out26), .Q(R26out), .clk(Clock));  // open: clr
  Register #(.width(32)) register_28 (.D(Data), .en(decoder_1_out27), .Q(R27out), .clk(Clock));  // open: clr
  Register #(.width(32)) register_29 (.D(Data), .en(decoder_1_out28), .Q(R28out), .clk(Clock));  // open: clr
  Register #(.width(32)) register_30 (.D(Data), .en(decoder_1_out29), .Q(R29out), .clk(Clock));  // open: clr
  Register #(.width(32)) register_31 (.D(Data), .en(decoder_1_out30), .Q(R30out), .clk(Clock));  // open: clr
  Register #(.width(32)) register_32 (.D(Data), .en(decoder_1_out31), .Q(R31out), .clk(Clock));  // open: clr
  Multiplexer #(.select(5), .width(32), .enable("false")) multiplexer_1 (
    .in0(R00out), .in1(R01out), .in2(R02out), .in3(R03out), .in4(R04out), .in5(R05out), .in6(R06out),
    .in7(R07out), .in8(R08out), .in9(R09out), .in10(R10out), .in11(R11out), .in12(R12out), .in13(R13out),
    .in14(R14out), .in15(R15out), .in16(R16out), .in17(R17out), .in18(R18out), .in19(R19out), .in20(R20out),
    .in21(R21out), .in22(R22out), .in23(R23out), .in24(R24out), .in25(R25out), .in26(R26out), .in27(R27out),
    .in28(R28out), .in29(R29out), .in30(R30out), .in31(R31out), .out(Output__1), .sel(Read__1_Selector));
  Multiplexer #(.select(5), .width(32), .enable("false")) multiplexer_2 (
    .in0(R00out), .in1(R01out), .in2(R02out), .in3(R03out), .in4(R04out), .in5(R05out), .in6(R06out),
    .in7(R07out), .in8(R08out), .in9(R09out), .in10(R10out), .in11(R11out), .in12(R12out), .in13(R13out),
    .in14(R14out), .in15(R15out), .in16(R16out), .in17(R17out), .in18(R18out), .in19(R19out), .in20(R20out),
    .in21(R21out), .in22(R22out), .in23(R23out), .in24(R24out), .in25(R25out), .in26(R26out), .in27(R27out),
    .in28(R28out), .in29(R29out), .in30(R30out), .in31(R31out), .out(Output__2), .sel(Read__2_Selector));
endmodule

module ALU (
  input  [3:0] Function,
  input  [31:0] Input__1,
  input  [31:0] Input__2,
  output [31:0] Output
);

  wire [4:0] bit_extender_1_out;
  wire [31:0] adder_1_out, and_1_out, divider_1_out, divider_1_rem, multiplier_1_out, negator_1_out,
       not_1_out, or_1_out, shifter_1_out, shifter_2_out, subtractor_1_out, xor_1_out;

  Subtractor #(.width(32)) subtractor_1 (.a(Input__1), .b(Input__2), .out(subtractor_1_out), .bin(1'b0));  // open: bout
  Adder #(.width(32)) adder_1 (.a(Input__1), .b(Input__2), .out(adder_1_out), .cin(1'b0));  // open: cout
  Shifter #(.width(32)) shifter_1 (.in(Input__1), .\dist (bit_extender_1_out), .out(shifter_1_out));
  Bit_Extender #(.in_width(32), .out_width(5)) bit_extender_1 (.in(Input__2), .out(bit_extender_1_out));
  Shifter #(.width(32), .shift("lr")) shifter_2 (.in(Input__1), .\dist (bit_extender_1_out), .out(shifter_2_out));
  Multiplier #(.width(32)) multiplier_1 (
    .a(Input__1), .b(Input__2), .out(multiplier_1_out), .cin({32{1'b0}}));  // open: cout
  Divider #(.width(32)) divider_1 (
    .a(Input__1), .b(Input__2), .out(divider_1_out), .upper({32{1'b0}}), .rem(divider_1_rem));
  assign and_1_out = Input__1 & Input__2;  // AND_Gate and_1, 32 bits wide
  assign or_1_out = Input__1 | Input__2;  // OR_Gate or_1, 32 bits wide
  assign xor_1_out = Input__1 ^ Input__2;  // XOR_Gate xor_1, 32 bits wide
  assign not_1_out = ~Input__1;  // NOT_Gate not_1, 32 bits wide
  Negator #(.width(32)) negator_1 (.in(Input__1), .out(negator_1_out));
  Multiplexer #(.select(4), .width(32), .enable("false")) multiplexer_1 (
    .in0(subtractor_1_out), .in1(adder_1_out), .in2(shifter_1_out), .in3(shifter_2_out),
    .in4(multiplier_1_out), .in5(divider_1_out), .in6(divider_1_rem), .in7(and_1_out), .in8(or_1_out),
    .in9(xor_1_out), .in10(not_1_out), .in11(negator_1_out), .in12({32{1'b0}}), .in13({32{1'b0}}),
    .in14(Input__2), .in15({Input__2[15:0], {16{1'b0}}}), .out(Output), .sel(Function));
endmodule

module PC (
  input  [2:0] Condition_Select,
  input  Greater,
  input  Equal,
  input  Less,
  input  [31:0] Address,
  input  [1:0] Load_Select,
  input  Enable,
  input  Clock,
  input  Reset,
  output [31:0] Q
);

  wire and_1_out, multiplexer_2_out, not_1_out, or_1_out, or_2_out;
  wire [31:0] adder_1_out, multiplexer_1_out, multiplexer_3_out;

  or or_1 (or_1_out, Greater, Equal);
  or or_2 (or_2_out, Equal, Less);
  Multiplexer #(.width(32), .enable("false")) multiplexer_1 (
    .in0(32'h1), .in1(Address), .out(multiplexer_1_out), .sel(Load_Select[1]));
  Multiplexer #(.select(3), .enable("false")) multiplexer_2 (
    .in0(1'b1), .in1(Greater), .in2(or_1_out), .in3(Equal), .in4(or_2_out), .in5(Less), .in6(not_1_out),
    .in7(1'b0), .out(multiplexer_2_out), .sel(Condition_Select));
  not not_1 (not_1_out, Equal);
  Adder #(.width(32)) adder_1 (.a(Q), .b(multiplexer_1_out), .out(adder_1_out), .cin(1'b0));  // open: cout
  and and_1 (and_1_out, Enable, multiplexer_2_out);
  Multiplexer #(.width(32), .enable("false")) multiplexer_3 (
    .in0(adder_1_out), .in1(Address), .out(multiplexer_3_out), .sel(Load_Select[0]));
  Register #(.width(32)) register_1 (.D(multiplexer_3_out), .en(and_1_out), .Q(Q), .clk(Clock), .clr(Reset));
endmodule

module IR (
  input  [31:0] D,
  input  Enable,
  input  Clock,
  output [3:0] AluFunction,
  output [5:0] OpCode,
  output [10:0] XtdOpCode,
  output [31:0] Q,
  output [4:0] RA,
  output [4:0] RB,
  output [4:0] RC,
  output [20:0] Address,
  output [15:0] Offset
);

  Register #(.width(32)) register_1 (.D(D), .en(Enable), .Q({OpCode, Q[25:21], Address}), .clk(Clock));  // open: clr

  assign AluFunction = Address[3:0];
  assign Offset = Address[15:0];
  assign {Q[31:26], Q[20:0]} = {OpCode, Address};
  assign RA = Q[25:21];
  assign RB = Address[20:16];
  assign RC = Address[15:11];
  assign XtdOpCode = Address[10:0];
endmodule

module ControlUnit (
  input  [5:0] OpCode,
  input  [10:0] XtdOpCode,
  input  Clk,
  input  _0,
  output [31:0] Q
);

  wire and_1_out;
  wire [7:0] bit_extender_1_out, MPC_q, multiplexer_1_out, multiplexer_2_out, rom_1_data;
  wire [31:0] rom_2_data;

  and and_1 (and_1_out, OpCode[0], OpCode[1], OpCode[2], OpCode[3], OpCode[4], OpCode[5]);
  assign bit_extender_1_out = {{2{1'b0}}, OpCode};  // Bit_Extender bit_extender_1
  Multiplexer #(.width(8), .enable("false")) multiplexer_1 (
    .in0(Q[29:22]), .in1(rom_1_data), .out(multiplexer_1_out), .sel(Q[31]));
  // Probe on multiplexer_1_out
  Multiplexer #(.width(8), .enable("false")) multiplexer_2 (
    .in0(bit_extender_1_out), .in1({2'b01, XtdOpCode[5:0]}), .out(multiplexer_2_out), .sel(and_1_out));
  // Probe on multiplexer_2_out
  Register MPC (.D(multiplexer_1_out), .Q(MPC_q), .clk(Clk), .clr(_0));  // open: en
  ROM rom_1 (.addr(multiplexer_2_out), .data(rom_1_data));  // open: sel
  ROM #(.dataWidth(32)) rom_2 (.addr(MPC_q), .data(rom_2_data));  // open: sel
  Register #(.width(32), .trigger("falling")) MIR (.D(rom_2_data), .Q(Q), .clk(Clk), .clr(_0));  // open: en
  // Probe on Q[29:22]

  // Notes on the sheet:
  //   contents of rom_1 (hex, n*v repeats v):
  //   3 0 4 6
  //   contents of rom_2 (hex, n*v repeats v):
  //   40004c a00001 80000000 c00000 1438024 80001
endmodule
